# Fritzing sketch fritzing-limbic-logo (saved by Fritzing 0.9.3b)
breadboards: 1

parts:
  LED1 = ws2812b [package="smd 2812b"]
  LED2 = ws2812b [package="smd 2812b"]
  LED4 = ws2812b [package="smd 2812b"]
  LED3 = ws2812b [package="smd 2812b"]
  LED5 = ws2812b [package="smd 2812b"]
  LED6 = ws2812b [package="smd 2812b"]
  LED7 = ws2812b [package="smd 2812b"]
  LED8 = ws2812b [package="smd 2812b"]
  LED13 = ws2812b [package="smd 2812b"]
  LED12 = ws2812b [package="smd 2812b"]
  LED10 = ws2812b [package="smd 2812b"]
  LED11 = ws2812b [package="smd 2812b"]
  LED14 = ws2812b [package="smd 2812b"]
  LED9 = ws2812b [package="smd 2812b"]
  LED15 = ws2812b [package="smd 2812b"]
  R1 = Resistor [tolerance=±5% resistance=220 package="2512 [SMD]"]
  C1 = Capacitor [package=0603-cap]
  C2 = Capacitor [package=0603-cap]
  C3 = Capacitor [package=0603-cap]
  C4 = Capacitor [package=0603-cap]
  C5 = Capacitor [package=0603-cap]
  C6 = Capacitor [package=0603-cap]
  C7 = Capacitor [package=0603-cap]
  C8 = Capacitor [package=0603-cap]
  C9 = Capacitor [package=0603-cap]
  C10 = Capacitor [package=0603-cap]
  C11 = Capacitor [package=0603-cap]
  C12 = Capacitor [package=0603-cap]
  C13 = Capacitor [package=0603-cap]
  C14 = Capacitor [package=0603-cap]
  C15 = Capacitor [package=0603-cap]
  Part2 = Particle P1 [package=P1]
  JP1 = USB_MICROB_PLUG [package=micro-b-ra-th]

nets:
  5V: LED1.VDD, LED2.VDD, LED4.VDD, LED3.VDD, LED5.VDD, LED6.VDD, LED7.VDD, LED8.VDD, LED13.VDD, LED12.VDD, LED10.VDD, LED11.VDD, LED14.VDD, LED9.VDD, LED15.VDD, C1.2, C2.2, C3.2, C4.2, C5.2, C6.2, C7.2, C8.2, C9.2, C10.2, C11.2, C12.2, C13.2, C14.2, C15.2, JP1.VCC
  N1: LED1.DOUT, LED2.DIN
  GND: LED1.VSS, LED2.VSS, LED4.VSS, LED3.VSS, LED5.VSS, LED6.VSS, LED7.VSS, LED8.VSS, LED13.VSS, LED12.VSS, LED10.VSS, LED11.VSS, LED14.VSS, LED9.VSS, LED15.VSS, C1.1, C2.1, C3.1, C4.1, C5.1, C6.1, C7.1, C8.1, C9.1, C10.1, C11.1, C12.1, C13.1, C14.1, C15.1, Part2.1, JP1.GND
  N2: LED1.DIN, R1.Pin_1
  N3: LED2.DOUT, LED3.DIN
  N4: LED4.DOUT, LED5.DIN
  N5: LED4.DIN, LED3.DOUT
  N6: LED5.DOUT, LED6.DIN
  N7: LED6.DOUT, LED7.DIN
  N8: LED7.DOUT, LED8.DIN
  N9: LED8.DOUT, LED9.DIN
  N10: LED13.DOUT, LED14.DIN
  N11: LED13.DIN, LED12.DOUT
  N12: LED12.DIN, LED11.DOUT
  N13: LED10.DOUT, LED11.DIN
  N14: LED10.DIN, LED9.DOUT
  N15: LED14.DOUT, LED15.DIN
  N16: R1.Pin_0, Part2.36
